# Fritzing sketch SketchHC595_SPI (saved by Fritzing 0.8.7b)
breadboards: 3

parts:
  U1 = atmega328 [package=dip]
  U2 = 74HC595 [package="DIP16 [THT]"]
  Componente1 = FTDI Basic Programmer  # not connected
  LED1 = smd LED [color="Red (633nm)" package="0805 [SMD]"]
  LED2 = smd LED [color="Red (633nm)" package="0805 [SMD]"]
  LED3 = smd LED [color="Red (633nm)" package="0805 [SMD]"]
  LED4 = smd LED [color="Red (633nm)" package="0805 [SMD]"]
  LED5 = smd LED [color="Red (633nm)" package="0805 [SMD]"]
  LED6 = smd LED [color="Red (633nm)" package="0805 [SMD]"]
  LED7 = smd LED [color="Red (633nm)" package="0805 [SMD]"]
  LED8 = smd LED [color="Red (633nm)" package="0805 [SMD]"]
  C1 = Electrolytic Capacitor [capacitance=1µF package="0807 [SMD, electrolytic]"]
  C2 = Capacitor [package=cap-pth-5mm]
  R1 = Resistor [tolerance=±5% resistance=220 package="1206 [SMD]"]
  R2 = Resistor [tolerance=±5% resistance=220 package="1206 [SMD]"]
  R3 = Resistor [tolerance=±5% resistance=220 package="1206 [SMD]"]
  R4 = Resistor [tolerance=±5% resistance=220 package="1206 [SMD]"]
  R6 = Resistor [tolerance=±5% resistance=220 package="1206 [SMD]"]
  R7 = Resistor [tolerance=±5% resistance=220 package="1206 [SMD]"]
  R8 = Resistor [tolerance=±5% resistance=220 package="1206 [SMD]"]
  R5 = Resistor [tolerance=±5% resistance=220 package="1206 [SMD]"]

nets:
  VCC: U1.VCC, U2.MR, U2.VCC, C2.1
  N1: U1.GND#7, U2.GND, U2.OE, LED1.cathode, LED2.cathode, LED3.cathode, LED4.cathode, LED5.cathode, LED6.cathode, LED7.cathode, LED8.cathode, C1.-, C2.2
  N2: U1.D9_(PWM), U2.ST_CP, C1.+
  N3: U1.D11_(PWM), U2.DS
  N4: U1.D13, U2.SH_CP
  N5: U2.Q1, R2.Pin_0
  N6: U2.Q2, R3.Pin_0
  N7: U2.Q3, R4.Pin_0
  N8: U2.Q4, R5.Pin_0
  N9: U2.Q5, R6.Pin_0
  N10: U2.Q6, R7.Pin_0
  N11: U2.Q7, R8.Pin_0
  N12: U2.Q0, R1.Pin_0
  N13: LED1.anode, R8.Pin_1
  N14: LED2.anode, R7.Pin_1
  N15: LED3.anode, R6.Pin_1
  N16: LED4.anode, R5.Pin_1
  N17: LED5.anode, R4.Pin_1
  N18: LED6.anode, R3.Pin_1
  N19: LED7.anode, R2.Pin_1
  N20: LED8.anode, R1.Pin_1
